// Logisim project avaliação2.circ as structural Verilog: 1 circuit, main circuit main
module main (
);

  wire and_1_out, and_2_out, b, button_4_out, button_5_out, button_6_out, clock_1_out, counter_1_carry,
       counter_2_carry, counter_3_carry, counter_4_carry, counter_5_carry, counter_6_carry, G_out,
       nand_1_out, not_1_out, not_2_out, not_3_out, not_4_out, not_5_out, or_2_out, or_3_out, R_out, T, t1,
       t2, t3, t_t;
  wire [3:0] _0, _1, _2, _3, _4, _5, controlled_buffer_25_out, controlled_buffer_26_out, counter_1_q,
       counter_2_q, counter_3_q, counter_4_q, counter_5_q, counter_6_q, register_1_q, register_2_q,
       register_3_q, register_4_q, register_5_q, register_6_q, register_7_q, register_8_q, register_9_q,
       register_10_q, register_11_q, register_12_q, register_13_q, register_14_q, register_15_q,
       register_16_q, register_17_q, register_18_q, register_19_q, register_20_q;

  assign _0 = t3 ? register_1_q : 4'bz;  // Controlled_Buffer controlled_buffer_1
  Register #(.width(4), .trigger("high")) register_1 (.D(register_2_q), .Q(register_1_q), .clk(b));  // open: en, clr
  assign _0 = t2 ? register_2_q : 4'bz;  // Controlled_Buffer controlled_buffer_2
  Register #(.width(4), .trigger("high")) register_2 (.D(register_3_q), .Q(register_2_q), .clk(b));  // open: en, clr
  assign _0 = t1 ? register_3_q : 4'bz;  // Controlled_Buffer controlled_buffer_3
  Register #(.width(4), .trigger("high")) register_3 (.D(_0), .Q(register_3_q), .clk(b));  // open: en, clr
  not not_1 (not_1_out, counter_3_q[0]);
  assign _1 = t3 ? register_4_q : 4'bz;  // Controlled_Buffer controlled_buffer_4
  Register #(.width(4), .trigger("high")) register_4 (.D(register_5_q), .Q(register_4_q), .clk(b));  // open: en, clr
  assign _1 = t2 ? register_5_q : 4'bz;  // Controlled_Buffer controlled_buffer_5
  Register #(.width(4), .trigger("high")) register_5 (.D(register_6_q), .Q(register_5_q), .clk(b));  // open: en, clr
  assign _1 = t1 ? register_6_q : 4'bz;  // Controlled_Buffer controlled_buffer_6
  Register #(.width(4), .trigger("high")) register_6 (.D(_1), .Q(register_6_q), .clk(b));  // open: en, clr
  not not_2 (not_2_out, counter_3_q[3]);
  not not_3 (not_3_out, counter_3_q[1]);
  not not_4 (not_4_out, counter_3_q[2]);
  nand nand_1 (nand_1_out, not_1_out, not_3_out, not_4_out, not_2_out, counter_1_carry);
  assign _2 = t3 ? register_7_q : 4'bz;  // Controlled_Buffer controlled_buffer_7
  assign _3 = t3 ? register_8_q : 4'bz;  // Controlled_Buffer controlled_buffer_8
  Register #(.width(4), .trigger("high")) register_7 (.D(register_9_q), .Q(register_7_q), .clk(b));  // open: en, clr
  Register #(.width(4), .trigger("high")) register_8 (.D(register_10_q), .Q(register_8_q), .clk(b));  // open: en, clr
  assign _2 = t2 ? register_9_q : 4'bz;  // Controlled_Buffer controlled_buffer_9
  assign _3 = t2 ? register_10_q : 4'bz;  // Controlled_Buffer controlled_buffer_10
  Register #(.width(4), .trigger("high")) register_9 (.D(register_11_q), .Q(register_9_q), .clk(b));  // open: en, clr
  Register #(.width(4), .trigger("high")) register_10 (.D(register_12_q), .Q(register_10_q), .clk(b));  // open: en, clr
  assign _2 = t1 ? register_11_q : 4'bz;  // Controlled_Buffer controlled_buffer_11
  assign _3 = t1 ? register_12_q : 4'bz;  // Controlled_Buffer controlled_buffer_12
  Register #(.width(4), .trigger("high")) register_11 (.D(_2), .Q(register_11_q), .clk(b));  // open: en, clr
  Register #(.width(4), .trigger("high")) register_12 (.D(_3), .Q(register_12_q), .clk(b));  // open: en, clr
  Hex_Digit_Display hex_digit_display_1 (.value(_0));  // open: dp
  Hex_Digit_Display hex_digit_display_2 (.value(_1));  // open: dp
  assign _0 = t_t ? counter_1_q : 4'bz;  // Controlled_Buffer controlled_buffer_13
  assign _1 = t_t ? counter_3_q : 4'bz;  // Controlled_Buffer controlled_buffer_14
  Counter #(.width(4), .max('h2), .trigger("falling")) counter_1 (
    .load(1'b1), .Q(counter_1_q), .carry(counter_1_carry), .clk(counter_3_carry), .clr(T));  // open: D, count
  assign _4 = t3 ? register_13_q : 4'bz;  // Controlled_Buffer controlled_buffer_15
  Register #(.width(4), .trigger("high")) register_13 (.D(register_14_q), .Q(register_13_q), .clk(b));  // open: en, clr
  assign _4 = t2 ? register_14_q : 4'bz;  // Controlled_Buffer controlled_buffer_16
  Register #(.width(4), .trigger("high")) register_14 (.D(register_15_q), .Q(register_14_q), .clk(b));  // open: en, clr
  assign _4 = t1 ? register_15_q : 4'bz;  // Controlled_Buffer controlled_buffer_17
  Register #(.width(4), .trigger("high")) register_15 (.D(_4), .Q(register_15_q), .clk(b));  // open: en, clr
  LED led_1 (.in(not_5_out));
  LED led_2 (.in(not_5_out));
  Hex_Digit_Display hex_digit_display_3 (.value(_2));  // open: dp
  assign _2 = t_t ? counter_2_q : 4'bz;  // Controlled_Buffer controlled_buffer_18
  Counter #(.width(4), .max('h5), .trigger("falling")) counter_2 (
    .load(1'b1), .Q(counter_2_q), .carry(counter_2_carry), .clk(counter_4_carry), .clr(T));  // open: D, count
  Counter #(.width(4), .max('h9), .trigger("falling")) counter_3 (
    .load(1'b1), .D(4'b0100), .count(nand_1_out), .Q(counter_3_q), .carry(counter_3_carry), .clk(and_1_out),
    .clr(T));
  and and_1 (and_1_out, counter_4_carry, counter_2_carry);
  assign _5 = t3 ? register_16_q : 4'bz;  // Controlled_Buffer controlled_buffer_19
  Register #(.width(4), .trigger("high")) register_16 (.D(register_17_q), .Q(register_16_q), .clk(b));  // open: en, clr
  assign _5 = t2 ? register_17_q : 4'bz;  // Controlled_Buffer controlled_buffer_20
  Register #(.width(4), .trigger("high")) register_17 (.D(register_18_q), .Q(register_17_q), .clk(b));  // open: en, clr
  assign _5 = t1 ? register_18_q : 4'bz;  // Controlled_Buffer controlled_buffer_21
  Register #(.width(4), .trigger("high")) register_18 (.D(_5), .Q(register_18_q), .clk(b));  // open: en, clr
  LED led_3 (.in(not_5_out));
  LED led_4 (.in(not_5_out));
  Hex_Digit_Display hex_digit_display_4 (.value(_3));  // open: dp
  assign _3 = t_t ? counter_4_q : 4'bz;  // Controlled_Buffer controlled_buffer_22
  Counter #(.width(4), .max('h9), .trigger("falling")) counter_4 (
    .load(1'b1), .Q(counter_4_q), .carry(counter_4_carry), .clk(and_2_out), .clr(T));  // open: D, count
  and and_2 (and_2_out, counter_6_carry, counter_5_carry);
  Button button_1 (.out(t3));
  Button button_2 (.out(t2));
  Button button_3 (.out(t1));
  not not_5 (not_5_out, clock_1_out);
  Hex_Digit_Display hex_digit_display_5 (.value(_4));  // open: dp
  Hex_Digit_Display hex_digit_display_6 (.value(_5));  // open: dp
  assign _5 = t_t ? counter_6_q : 4'bz;  // Controlled_Buffer controlled_buffer_23
  assign _4 = t_t ? counter_5_q : 4'bz;  // Controlled_Buffer controlled_buffer_24
  Counter #(.width(4), .max('h5), .trigger("falling")) counter_5 (
    .load(1'b1), .Q(counter_5_q), .carry(counter_5_carry), .clk(counter_6_carry), .clr(T));  // open: D, count
  assign controlled_buffer_25_out = R_out ? 4'b0000 : 4'bz;  // Controlled_Buffer controlled_buffer_25
  Button R (.out(R_out));
  Button G (.out(G_out));
  Counter #(.width(4), .max('h9), .trigger("falling")) counter_6 (
    .load(1'b1), .Q(counter_6_q), .carry(counter_6_carry), .clk(clock_1_out), .clr(T));  // open: D, count
  Clock clock_1 (.out(clock_1_out));
  buf buffer_1 (T, R_out);
  assign _5 = controlled_buffer_25_out;  // Buffer buffer_2, 4 bits wide
  assign _4 = controlled_buffer_25_out;  // Buffer buffer_3, 4 bits wide
  assign _3 = controlled_buffer_25_out;  // Buffer buffer_4, 4 bits wide
  assign _2 = controlled_buffer_25_out;  // Buffer buffer_5, 4 bits wide
  assign _1 = controlled_buffer_25_out;  // Buffer buffer_6, 4 bits wide
  assign _0 = controlled_buffer_25_out;  // Buffer buffer_7, 4 bits wide
  or or_1 (b, R_out, G_out);
  or or_2 (or_2_out, t1, t2, t3, R_out);
  not not_6 (t_t, or_2_out);
  Button button_4 (.out(button_4_out));
  Button button_5 (.out(button_5_out));
  // Probe on controlled_buffer_26_out
  assign controlled_buffer_26_out = button_4_out ? 4'b0001 : 4'bz;  // Controlled_Buffer controlled_buffer_26
  assign controlled_buffer_26_out = button_5_out ? 4'b0010 : 4'bz;  // Controlled_Buffer controlled_buffer_27
  Register #(.width(4), .trigger("high")) register_19 (
    .D(controlled_buffer_26_out), .Q(register_19_q), .clk(or_3_out), .clr(button_6_out));  // open: en
  or or_3 (or_3_out, button_4_out, button_5_out);
  Hex_Digit_Display hex_digit_display_7 (.value(register_20_q));  // open: dp
  Register #(.width(4)) register_20 (
    .D(register_19_q), .Q(register_20_q), .clk(or_3_out), .clr(button_6_out));  // open: en
  Hex_Digit_Display hex_digit_display_8 (.value(register_19_q));  // open: dp
  Button button_6 (.out(button_6_out));
endmodule
