// Logisim project avaliação2_arqo.circ as structural Verilog: 4 circuits, main circuit main
module main (
);

  wire and_1_out, and_2_out, and_4_out, and_5_out, b, clock_1_out, counter_2_carry, counter_3_carry,
       counter_4_carry, counter_5_carry, counter_6_carry, G_out, not_1_out, not_2_out, not_3_out, or_2_out,
       r1, r2, r3, R_out, T, t1, t2, t3, t_t;
  wire [1:0] counter_7_q;
  wire [3:0] _0, _1, _2, _3, _4, _5, controlled_buffer_25_out, counter_1_q, counter_2_q, counter_3_q,
       counter_4_q, counter_5_q, counter_6_q, register_1_q, register_2_q, register_3_q, register_4_q,
       register_5_q, register_6_q, register_7_q, register_8_q, register_9_q, register_10_q, register_11_q,
       register_12_q, register_13_q, register_14_q, register_15_q, register_16_q, register_17_q,
       register_18_q;

  Register #(.width(4), .trigger("high")) register_1 (
    .D(register_2_q), .en(r1), .Q(register_1_q), .clk(b));  // open: clr
  Register #(.width(4), .trigger("high")) register_2 (
    .D(register_3_q), .en(r2), .Q(register_2_q), .clk(b));  // open: clr
  Register #(.width(4), .trigger("high")) register_3 (.D(_0), .en(r3), .Q(register_3_q), .clk(b));  // open: clr
  Hex_Digit_Display hex_digit_display_1 (.value(_0));  // open: dp
  assign _0 = t_t ? counter_1_q : 4'bz;  // Controlled_Buffer controlled_buffer_1
  Counter #(.width(4), .max('h2), .trigger("falling")) counter_1 (
    .load(1'b1), .Q(counter_1_q), .clk(counter_2_carry), .clr(T));  // open: D, count, carry
  assign _1 = t3 ? register_4_q : 4'bz;  // Controlled_Buffer controlled_buffer_2
  assign _0 = t3 ? register_1_q : 4'bz;  // Controlled_Buffer controlled_buffer_3
  Register #(.width(4), .trigger("high")) register_4 (
    .D(register_5_q), .en(r1), .Q(register_4_q), .clk(b));  // open: clr
  assign _0 = t2 ? register_2_q : 4'bz;  // Controlled_Buffer controlled_buffer_4
  assign _1 = t2 ? register_5_q : 4'bz;  // Controlled_Buffer controlled_buffer_5
  Register #(.width(4), .trigger("high")) register_5 (
    .D(register_6_q), .en(r2), .Q(register_5_q), .clk(b));  // open: clr
  assign _0 = t1 ? register_3_q : 4'bz;  // Controlled_Buffer controlled_buffer_6
  assign _1 = t1 ? register_6_q : 4'bz;  // Controlled_Buffer controlled_buffer_7
  Register #(.width(4), .trigger("high")) register_6 (.D(_1), .en(r3), .Q(register_6_q), .clk(b));  // open: clr
  LED led_1 (.in(not_1_out));
  LED led_2 (.in(not_1_out));
  Hex_Digit_Display hex_digit_display_2 (.value(_1));  // open: dp
  assign _1 = t_t ? counter_2_q : 4'bz;  // Controlled_Buffer controlled_buffer_8
  Counter #(.width(4), .max('h9), .trigger("falling")) counter_2 (
    .load(1'b1), .Q(counter_2_q), .carry(counter_2_carry), .clk(and_1_out), .clr(T));  // open: D, count
  and and_1 (and_1_out, counter_4_carry, counter_3_carry);
  assign _2 = t3 ? register_7_q : 4'bz;  // Controlled_Buffer controlled_buffer_9
  Register #(.width(4), .trigger("high")) register_7 (
    .D(register_8_q), .en(r1), .Q(register_7_q), .clk(b));  // open: clr
  assign _2 = t2 ? register_8_q : 4'bz;  // Controlled_Buffer controlled_buffer_10
  Register #(.width(4), .trigger("high")) register_8 (
    .D(register_9_q), .en(r2), .Q(register_8_q), .clk(b));  // open: clr
  assign _2 = t1 ? register_9_q : 4'bz;  // Controlled_Buffer controlled_buffer_11
  Register #(.width(4), .trigger("high")) register_9 (.D(_2), .en(r3), .Q(register_9_q), .clk(b));  // open: clr
  Hex_Digit_Display hex_digit_display_3 (.value(_2));  // open: dp
  Hex_Digit_Display hex_digit_display_4 (.value(_3));  // open: dp
  assign _2 = t_t ? counter_3_q : 4'bz;  // Controlled_Buffer controlled_buffer_12
  assign _3 = t_t ? counter_4_q : 4'bz;  // Controlled_Buffer controlled_buffer_13
  Counter #(.width(4), .max('h5), .trigger("falling")) counter_3 (
    .load(1'b1), .Q(counter_3_q), .carry(counter_3_carry), .clk(counter_4_carry), .clr(T));  // open: D, count
  assign _3 = t3 ? register_11_q : 4'bz;  // Controlled_Buffer controlled_buffer_14
  Register #(.width(4), .trigger("high")) register_10 (
    .D(register_12_q), .en(r1), .Q(register_10_q), .clk(b));  // open: clr
  Register #(.width(4), .trigger("high")) register_11 (
    .D(register_13_q), .en(r1), .Q(register_11_q), .clk(b));  // open: clr
  assign _3 = t2 ? register_13_q : 4'bz;  // Controlled_Buffer controlled_buffer_15
  Register #(.width(4), .trigger("high")) register_12 (
    .D(register_14_q), .en(r2), .Q(register_12_q), .clk(b));  // open: clr
  Register #(.width(4), .trigger("high")) register_13 (
    .D(register_15_q), .en(r2), .Q(register_13_q), .clk(b));  // open: clr
  assign _3 = t1 ? register_15_q : 4'bz;  // Controlled_Buffer controlled_buffer_16
  Register #(.width(4), .trigger("high")) register_14 (.D(_4), .en(r3), .Q(register_14_q), .clk(b));  // open: clr
  Register #(.width(4), .trigger("high")) register_15 (.D(_3), .en(r3), .Q(register_15_q), .clk(b));  // open: clr
  LED led_3 (.in(not_1_out));
  LED led_4 (.in(not_1_out));
  Hex_Digit_Display hex_digit_display_5 (.value(_4));  // open: dp
  assign _4 = t_t ? counter_6_q : 4'bz;  // Controlled_Buffer controlled_buffer_17
  Counter #(.width(4), .max('h9), .trigger("falling")) counter_4 (
    .load(1'b1), .Q(counter_4_q), .carry(counter_4_carry), .clk(and_2_out), .clr(T));  // open: D, count
  and and_2 (and_2_out, counter_5_carry, counter_6_carry);
  assign _5 = t3 ? register_16_q : 4'bz;  // Controlled_Buffer controlled_buffer_18
  assign _4 = t3 ? register_10_q : 4'bz;  // Controlled_Buffer controlled_buffer_19
  Register #(.width(4), .trigger("high")) register_16 (
    .D(register_17_q), .en(r1), .Q(register_16_q), .clk(b));  // open: clr
  assign _5 = t2 ? register_17_q : 4'bz;  // Controlled_Buffer controlled_buffer_20
  assign _4 = t2 ? register_12_q : 4'bz;  // Controlled_Buffer controlled_buffer_21
  Register #(.width(4), .trigger("high")) register_17 (
    .D(register_18_q), .en(r2), .Q(register_17_q), .clk(b));  // open: clr
  assign _5 = t1 ? register_18_q : 4'bz;  // Controlled_Buffer controlled_buffer_22
  assign _4 = t1 ? register_14_q : 4'bz;  // Controlled_Buffer controlled_buffer_23
  Register #(.width(4), .trigger("high")) register_18 (.D(_5), .en(r3), .Q(register_18_q), .clk(b));  // open: clr
  not not_1 (not_1_out, clock_1_out);
  Hex_Digit_Display hex_digit_display_6 (.value(_5));  // open: dp
  assign _5 = t_t ? counter_5_q : 4'bz;  // Controlled_Buffer controlled_buffer_24
  Counter #(.width(4), .max('h9), .trigger("falling")) counter_5 (
    .load(1'b1), .Q(counter_5_q), .carry(counter_5_carry), .clk(clock_1_out), .clr(T));  // open: D, count
  Counter #(.width(4), .max('h5), .trigger("falling")) counter_6 (
    .load(1'b1), .Q(counter_6_q), .carry(counter_6_carry), .clk(counter_5_carry), .clr(T));  // open: D, count
  Button u_T1 (.out(t3));
  Button u_T2 (.out(t2));
  Button u_T3 (.out(t1));
  Clock clock_1 (.out(clock_1_out));
  assign controlled_buffer_25_out = R_out ? 4'b0000 : 4'bz;  // Controlled_Buffer controlled_buffer_25
  Button R (.out(R_out));
  Button G (.out(G_out));
  buf buffer_1 (T, R_out);
  assign _5 = controlled_buffer_25_out;  // Buffer buffer_2, 4 bits wide
  assign _4 = controlled_buffer_25_out;  // Buffer buffer_3, 4 bits wide
  assign _3 = controlled_buffer_25_out;  // Buffer buffer_4, 4 bits wide
  assign _2 = controlled_buffer_25_out;  // Buffer buffer_5, 4 bits wide
  assign _1 = controlled_buffer_25_out;  // Buffer buffer_6, 4 bits wide
  assign _0 = controlled_buffer_25_out;  // Buffer buffer_7, 4 bits wide
  or or_1 (b, R_out, G_out);
  Counter #(.width(2), .max('h2), .trigger("falling")) counter_7 (
    .Q(counter_7_q), .clk(G_out), .clr(R_out));  // open: load, D, count, carry
  not not_2 (not_2_out, counter_7_q[0]);
  not not_3 (not_3_out, counter_7_q[1]);
  or or_2 (or_2_out, t1, t2, t3, R_out);
  not not_4 (t_t, or_2_out);
  and and_3 (r1, not_2_out, not_3_out);
  and and_4 (and_4_out, counter_7_q[0], not_3_out);
  and and_5 (and_5_out, not_2_out, counter_7_q[1]);
  or or_3 (r2, and_4_out, r1);
  or or_4 (r3, and_5_out, r2);
endmodule

module registradores (
);

  wire b, r1, r2, r3, t1, t2, t3;
  wire [3:0] _0, _1, _2, _3, _4, _5, register_1_q, register_2_q, register_3_q, register_4_q, register_5_q,
       register_6_q, register_7_q, register_8_q, register_9_q, register_10_q, register_11_q, register_12_q,
       register_13_q, register_14_q, register_15_q, register_16_q, register_17_q, register_18_q;

  Register #(.width(4), .trigger("high")) register_1 (
    .D(register_2_q), .en(r1), .Q(register_1_q), .clk(b));  // open: clr
  Register #(.width(4), .trigger("high")) register_2 (
    .D(register_3_q), .en(r2), .Q(register_2_q), .clk(b));  // open: clr
  Register #(.width(4), .trigger("high")) register_3 (.D(_0), .en(r3), .Q(register_3_q), .clk(b));  // open: clr
  assign _1 = t3 ? register_4_q : 4'bz;  // Controlled_Buffer controlled_buffer_1
  assign _0 = t3 ? register_1_q : 4'bz;  // Controlled_Buffer controlled_buffer_2
  Register #(.width(4), .trigger("high")) register_4 (
    .D(register_5_q), .en(r1), .Q(register_4_q), .clk(b));  // open: clr
  assign _0 = t2 ? register_2_q : 4'bz;  // Controlled_Buffer controlled_buffer_3
  assign _1 = t2 ? register_5_q : 4'bz;  // Controlled_Buffer controlled_buffer_4
  Register #(.width(4), .trigger("high")) register_5 (
    .D(register_6_q), .en(r2), .Q(register_5_q), .clk(b));  // open: clr
  assign _1 = t1 ? register_6_q : 4'bz;  // Controlled_Buffer controlled_buffer_5
  assign _0 = t1 ? register_3_q : 4'bz;  // Controlled_Buffer controlled_buffer_6
  Register #(.width(4), .trigger("high")) register_6 (.D(_1), .en(r3), .Q(register_6_q), .clk(b));  // open: clr
  assign _2 = t3 ? register_7_q : 4'bz;  // Controlled_Buffer controlled_buffer_7
  Register #(.width(4), .trigger("high")) register_7 (
    .D(register_8_q), .en(r1), .Q(register_7_q), .clk(b));  // open: clr
  assign _2 = t2 ? register_8_q : 4'bz;  // Controlled_Buffer controlled_buffer_8
  Register #(.width(4), .trigger("high")) register_8 (
    .D(register_9_q), .en(r2), .Q(register_8_q), .clk(b));  // open: clr
  assign _2 = t1 ? register_9_q : 4'bz;  // Controlled_Buffer controlled_buffer_9
  Register #(.width(4), .trigger("high")) register_9 (.D(_2), .en(r3), .Q(register_9_q), .clk(b));  // open: clr
  assign _3 = t3 ? register_11_q : 4'bz;  // Controlled_Buffer controlled_buffer_10
  Register #(.width(4), .trigger("high")) register_10 (
    .D(register_12_q), .en(r1), .Q(register_10_q), .clk(b));  // open: clr
  Register #(.width(4), .trigger("high")) register_11 (
    .D(register_13_q), .en(r1), .Q(register_11_q), .clk(b));  // open: clr
  assign _3 = t2 ? register_13_q : 4'bz;  // Controlled_Buffer controlled_buffer_11
  Register #(.width(4), .trigger("high")) register_12 (
    .D(register_14_q), .en(r2), .Q(register_12_q), .clk(b));  // open: clr
  Register #(.width(4), .trigger("high")) register_13 (
    .D(register_15_q), .en(r2), .Q(register_13_q), .clk(b));  // open: clr
  assign _3 = t1 ? register_15_q : 4'bz;  // Controlled_Buffer controlled_buffer_12
  Register #(.width(4), .trigger("high")) register_14 (.D(_4), .en(r3), .Q(register_14_q), .clk(b));  // open: clr
  Register #(.width(4), .trigger("high")) register_15 (.D(_3), .en(r3), .Q(register_15_q), .clk(b));  // open: clr
  assign _4 = t3 ? register_10_q : 4'bz;  // Controlled_Buffer controlled_buffer_13
  assign _5 = t3 ? register_16_q : 4'bz;  // Controlled_Buffer controlled_buffer_14
  Register #(.width(4), .trigger("high")) register_16 (
    .D(register_17_q), .en(r1), .Q(register_16_q), .clk(b));  // open: clr
  assign _5 = t2 ? register_17_q : 4'bz;  // Controlled_Buffer controlled_buffer_15
  assign _4 = t2 ? register_12_q : 4'bz;  // Controlled_Buffer controlled_buffer_16
  Register #(.width(4), .trigger("high")) register_17 (
    .D(register_18_q), .en(r2), .Q(register_17_q), .clk(b));  // open: clr
  assign _5 = t1 ? register_18_q : 4'bz;  // Controlled_Buffer controlled_buffer_17
  assign _4 = t1 ? register_14_q : 4'bz;  // Controlled_Buffer controlled_buffer_18
  Register #(.width(4), .trigger("high")) register_18 (.D(_5), .en(r3), .Q(register_18_q), .clk(b));  // open: clr
  Button u_T1 (.out(t3));
  Button u_T2 (.out(t2));
  Button u_T3 (.out(t1));
endmodule

module botoes (
);

  wire and_2_out, and_3_out, b, G_out, not_1_out, not_2_out, or_2_out, r1, r2, r3, R_out, T, t1, t2, t3, t_t;
  wire [1:0] counter_1_q;
  wire [3:0] _0, _1, _2, _3, _4, _5, controlled_buffer_1_out;

  assign controlled_buffer_1_out = R_out ? 4'b0000 : 4'bz;  // Controlled_Buffer controlled_buffer_1
  Button R (.out(R_out));
  Button G (.out(G_out));
  buf buffer_1 (T, R_out);
  assign _5 = controlled_buffer_1_out;  // Buffer buffer_2, 4 bits wide
  assign _4 = controlled_buffer_1_out;  // Buffer buffer_3, 4 bits wide
  assign _3 = controlled_buffer_1_out;  // Buffer buffer_4, 4 bits wide
  assign _2 = controlled_buffer_1_out;  // Buffer buffer_5, 4 bits wide
  assign _1 = controlled_buffer_1_out;  // Buffer buffer_6, 4 bits wide
  assign _0 = controlled_buffer_1_out;  // Buffer buffer_7, 4 bits wide
  or or_1 (b, R_out, G_out);
  Counter #(.width(2), .max('h2), .trigger("falling")) counter_1 (
    .Q(counter_1_q), .clk(G_out), .clr(R_out));  // open: load, D, count, carry
  not not_1 (not_1_out, counter_1_q[0]);
  not not_2 (not_2_out, counter_1_q[1]);
  not not_3 (t_t, or_2_out);
  or or_2 (or_2_out, t1, t2, t3, R_out);
  and and_1 (r1, not_1_out, not_2_out);
  and and_2 (and_2_out, counter_1_q[0], not_2_out);
  and and_3 (and_3_out, not_1_out, counter_1_q[1]);
  or or_3 (r2, and_2_out, r1);
  or or_4 (r3, and_3_out, r2);
endmodule

module timer (
);

  wire and_1_out, and_2_out, clock_1_out, counter_2_carry, counter_3_carry, counter_4_carry, counter_5_carry,
       counter_6_carry, not_1_out, T, t_t;
  wire [3:0] _0, _1, _2, _3, _4, _5, counter_1_q, counter_2_q, counter_3_q, counter_4_q, counter_5_q,
       counter_6_q;

  Hex_Digit_Display hex_digit_display_1 (.value(_0));  // open: dp
  assign _0 = t_t ? counter_1_q : 4'bz;  // Controlled_Buffer controlled_buffer_1
  Counter #(.width(4), .max('h2), .trigger("falling")) counter_1 (
    .load(1'b1), .Q(counter_1_q), .clk(counter_2_carry), .clr(T));  // open: D, count, carry
  LED led_1 (.in(not_1_out));
  LED led_2 (.in(not_1_out));
  Hex_Digit_Display hex_digit_display_2 (.value(_1));  // open: dp
  assign _1 = t_t ? counter_2_q : 4'bz;  // Controlled_Buffer controlled_buffer_2
  Counter #(.width(4), .max('h9), .trigger("falling")) counter_2 (
    .load(1'b1), .Q(counter_2_q), .carry(counter_2_carry), .clk(and_1_out), .clr(T));  // open: D, count
  and and_1 (and_1_out, counter_4_carry, counter_3_carry);
  Hex_Digit_Display hex_digit_display_3 (.value(_2));  // open: dp
  Hex_Digit_Display hex_digit_display_4 (.value(_3));  // open: dp
  assign _3 = t_t ? counter_4_q : 4'bz;  // Controlled_Buffer controlled_buffer_3
  assign _2 = t_t ? counter_3_q : 4'bz;  // Controlled_Buffer controlled_buffer_4
  Counter #(.width(4), .max('h5), .trigger("falling")) counter_3 (
    .load(1'b1), .Q(counter_3_q), .carry(counter_3_carry), .clk(counter_4_carry), .clr(T));  // open: D, count
  LED led_3 (.in(not_1_out));
  LED led_4 (.in(not_1_out));
  Hex_Digit_Display hex_digit_display_5 (.value(_4));  // open: dp
  assign _4 = t_t ? counter_6_q : 4'bz;  // Controlled_Buffer controlled_buffer_5
  Counter #(.width(4), .max('h9), .trigger("falling")) counter_4 (
    .load(1'b1), .Q(counter_4_q), .carry(counter_4_carry), .clk(and_2_out), .clr(T));  // open: D, count
  and and_2 (and_2_out, counter_5_carry, counter_6_carry);
  not not_1 (not_1_out, clock_1_out);
  Hex_Digit_Display hex_digit_display_6 (.value(_5));  // open: dp
  assign _5 = t_t ? counter_5_q : 4'bz;  // Controlled_Buffer controlled_buffer_6
  Counter #(.width(4), .max('h9), .trigger("falling")) counter_5 (
    .load(1'b1), .Q(counter_5_q), .carry(counter_5_carry), .clk(clock_1_out), .clr(T));  // open: D, count
  Counter #(.width(4), .max('h5), .trigger("falling")) counter_6 (
    .load(1'b1), .Q(counter_6_q), .carry(counter_6_carry), .clk(counter_5_carry), .clr(T));  // open: D, count
  Clock clock_1 (.out(clock_1_out));
endmodule
