// Logisim project circuitoteste1.circ as structural Verilog: 1 circuit, main circuit main
module main (
);

  wire A, and_1_out, clock_1_out;
  wire [2:0] counter_1_q;

  Clock clock_1 (.out(clock_1_out));
  // Probe on clock_1_out
  Counter #(.width(3), .max('h7)) counter_1 (
    .Q(counter_1_q), .clk(clock_1_out), .clr(and_1_out));  // open: load, D, count, carry
  LED led_1 (.in(A));
  LED led_2 (.in(A));
  LED led_3 (.in(A));
  LED led_4 (.in(A));
  // Probe on counter_1_q
  Register #(.width(3)) register_1 (.D(counter_1_q), .clk(A));  // open: en, Q, clr
  Button button_1 (.out(A));
  and and_1 (and_1_out, counter_1_q[2], counter_1_q[1], counter_1_q[0]);
endmodule
