// Logisim project exercicios.circ as structural Verilog: 1 circuit, main circuit main
module main (
);

  wire and_1_out, and_2_out, and_3_out, and_4_out, and_5_out, button_1_out, button_2_out, clock_1_out,
       clock_2_out, clock_3_out, clock_4_out, clock_5_out, clock_6_out, counter_3_carry, counter_4_carry,
       counter_5_carry, counter_6_carry, counter_7_carry, counter_8_carry, decoder_1_out0, decoder_1_out1,
       decoder_1_out2, decoder_1_out3, decoder_2_out0, decoder_2_out1, decoder_2_out2, decoder_2_out3,
       not_1_out, not_2_out, not_3_out;
  wire [1:0] counter_1_q, counter_2_q;
  wire [3:0] counter_3_q, counter_4_q, counter_5_q, counter_6_q, counter_7_q, counter_8_q;

  Button button_1 (.out(button_1_out));
  Clock clock_1 (.out(clock_1_out));
  Button button_2 (.out(button_2_out));
  Clock clock_2 (.out(clock_2_out));
  Clock clock_3 (.out(clock_3_out));
  Counter #(.width(2), .max('h3)) counter_1 (.Q(counter_1_q), .clk(clock_4_out));  // open: load, D, count, carry, clr
  Clock clock_4 (.out(clock_4_out));
  not not_1 (not_1_out, button_2_out);
  // Probe on counter_1_q
  and and_1 (and_1_out, button_1_out, clock_1_out);
  LED led_1 (.in(and_1_out));
  LED led_2 (.in(and_2_out));
  and and_2 (and_2_out, not_1_out, clock_2_out);
  LED led_3 (.in(not_2_out));
  not not_2 (not_2_out, clock_3_out);
  LED led_4 (.in(clock_3_out));
  LED led_5 (.in(decoder_1_out0));
  LED led_6 (.in(decoder_1_out1));
  LED led_7 (.in(decoder_1_out2));
  LED led_8 (.in(decoder_1_out3));
  Decoder #(.select(2)) decoder_1 (
    .out0(decoder_1_out0), .out1(decoder_1_out1), .out2(decoder_1_out2), .out3(decoder_1_out3),
    .sel(counter_1_q), .en(1'b1));
  Counter #(.width(2), .max('h3)) counter_2 (.Q(counter_2_q), .clk(clock_5_out));  // open: load, D, count, carry, clr
  Clock clock_5 (.out(clock_5_out));
  and and_3 (and_3_out, counter_4_q[2], counter_3_carry);
  // Probe on counter_2_q
  Hex_Digit_Display hex_digit_display_1 (.value(counter_3_q));  // open: dp
  Hex_Digit_Display hex_digit_display_2 (.value(counter_4_q));  // open: dp
  Counter #(.width(4), .max('h2), .trigger("falling")) counter_3 (
    .Q(counter_3_q), .carry(counter_3_carry), .clk(counter_4_carry), .clr(and_3_out));  // open: load, D, count
  and and_4 (and_4_out, counter_6_carry, counter_5_carry);
  LED led_9 (.in(decoder_2_out1));
  LED led_10 (.in(decoder_2_out0));
  LED led_11 (.in(decoder_2_out2));
  Decoder #(.select(2)) decoder_2 (
    .out0(decoder_2_out0), .out1(decoder_2_out1), .out2(decoder_2_out2), .out3(decoder_2_out3),
    .sel(counter_2_q), .en(1'b1));
  LED led_12 (.in(not_3_out));
  LED led_13 (.in(not_3_out));
  Hex_Digit_Display hex_digit_display_3 (.value(counter_5_q));  // open: dp
  Counter #(.width(4), .max('h9), .trigger("falling")) counter_4 (
    .Q(counter_4_q), .carry(counter_4_carry), .clk(and_4_out), .clr(and_3_out));  // open: load, D, count
  Counter #(.width(4), .max('h5), .trigger("falling")) counter_5 (
    .Q(counter_5_q), .carry(counter_5_carry), .clk(counter_6_carry));  // open: load, D, count, clr
  LED led_14 (.in(decoder_2_out3));
  LED led_15 (.in(decoder_2_out3));
  LED led_16 (.in(decoder_2_out1));
  LED led_17 (.in(decoder_2_out2));
  LED led_18 (.in(not_3_out));
  LED led_19 (.in(not_3_out));
  Hex_Digit_Display hex_digit_display_4 (.value(counter_6_q));  // open: dp
  Counter #(.width(4), .max('h9), .trigger("falling")) counter_6 (
    .Q(counter_6_q), .carry(counter_6_carry), .clk(and_5_out));  // open: load, D, count, clr
  and and_5 (and_5_out, counter_7_carry, counter_8_carry);
  Clock clock_6 (.out(clock_6_out));
  LED led_20 (.in(decoder_2_out0));
  not not_3 (not_3_out, clock_6_out);
  Hex_Digit_Display hex_digit_display_5 (.value(counter_7_q));  // open: dp
  Hex_Digit_Display hex_digit_display_6 (.value(counter_8_q));  // open: dp
  Counter #(.width(4), .max('h5), .trigger("falling")) counter_7 (
    .Q(counter_7_q), .carry(counter_7_carry), .clk(counter_8_carry));  // open: load, D, count, clr
  Counter #(.width(4), .max('h9), .trigger("falling")) counter_8 (
    .Q(counter_8_q), .carry(counter_8_carry), .clk(clock_6_out));  // open: load, D, count, clr
endmodule
